// Logisim project Circuito.circ as structural Verilog: 1 circuit, main circuit main
module main (
  input  SelRA1,
  input  SelRA2,
  input  SelRB1,
  input  SelRB2,
  output VA,
  output VB
);

  wire and_1_out, and_2_out, and_3_out, and_4_out, and_5_out, and_6_out, and_7_out, and_8_out, RA00_out,
       RA01_out, RA10_out, RA11_out, RB00_out, RB01_out, RB10_out, RB11_out;
  wire [7:0] R0_q, R1_q, R2_q, R3_q;

  Register R0 (.Q(R0_q));  // open: D, en, clk, clr
  Register R1 (.Q(R1_q));  // open: D, en, clk, clr
  Register R2 (.Q(R2_q));  // open: D, en, clk, clr
  Register R3 (.Q(R3_q));  // open: D, en, clk, clr
  and RA00 (RA00_out, ~SelRA1, ~SelRA2);  // AND_Gate
  and RA01 (RA01_out, ~SelRA1, SelRA2);  // AND_Gate
  and RA10 (RA10_out, SelRA1, ~SelRA2);  // AND_Gate
  and RA11 (RA11_out, SelRA1, SelRA2);
  and and_1 (and_1_out, RA00_out, R0_q[0]);
  and and_2 (and_2_out, RA01_out, R1_q[0]);
  and and_3 (and_3_out, RA10_out, R2_q[0]);
  and and_4 (and_4_out, RA11_out, R3_q[0]);
  and RB00 (RB00_out, ~SelRB1, ~SelRB2);  // AND_Gate
  and RB01 (RB01_out, ~SelRB1, SelRB2);  // AND_Gate
  and RB10 (RB10_out, SelRB1, ~SelRB2);  // AND_Gate
  and RB11 (RB11_out, SelRB1, SelRB2);
  and and_5 (and_5_out, RB00_out, R0_q[0]);
  and and_6 (and_6_out, RB01_out, R1_q[0]);
  and and_7 (and_7_out, RB10_out, R2_q[0]);
  and and_8 (and_8_out, RB11_out, R3_q[0]);
  or or_1 (VA, and_1_out, and_2_out, and_3_out, and_4_out);
  or or_2 (VB, and_5_out, and_6_out, and_7_out, and_8_out);
  // Pins of 1 and 8 bits meet at R0_q
  // Pins of 1 and 8 bits meet at R1_q
  // Pins of 1 and 8 bits meet at R2_q
  // Pins of 1 and 8 bits meet at R3_q
endmodule
