// Digital circuit MaquinaDeEstados.dig as structural Verilog
module MaquinaDeEstados (
  input  B,
  input  S,
  input  Reset,
  input  Clock,
  output F,
  output A,
  output SF,
  output SA
);

  portao #(.applicationType("GHDL")) u_portao (
    .KEY3(B), .KEY2(S), .KEY1(Reset), .KEY0(Clock), .LEDG7(F), .LEDG6(A), .LEDG1(SF), .LEDG0(SA));

  // Notes on the sheet:
  //   B: KEY(3)
  //   S: KEY(2)
  //   Reset: KEY(1)
  //   Clock: KEY(0)
  //   F: F
  //   A: A
  //   SF: SF
  //   SA: SA
endmodule

/* Code of portao:
LIBRARY ieee;
USE ieee.std_logic_1164.ALL;

ENTITY portao IS PORT (

 
	------ Variáveis ------
	--KEY: in STD_LOGIC_VECTOR(3 downto 0);
	KEY3: in STD_LOGIC;
	KEY2: in STD_LOGIC;
	KEY1: in STD_LOGIC;
	KEY0: in STD_LOGIC;

	--LEDG: out STD_LOGIC_VECTOR(7 downto 0)
	LEDG7: out STD_LOGIC;
	LEDG6: out STD_LOGIC;
	LEDG1: out STD_LOGIC;
	LEDG0: out STD_LOGIC

	);
END ENTITY portao;

ARCHITECTURE behave OF portao IS
	TYPE tipo_estado IS (Ab,c1,c2,Fc);
	signal estado : tipo_estado;
	signal A: STD_LOGIC;
	signal F: STD_LOGIC;
	BEGIN
		process(KEY3, KEY1, KEY0) begin -- Reset e Clock 
		-- Process Referente à transição de estados do sistema --
			if(KEY1 = '1') then --Reset
				estado <= Fc;
			elsif(KEY3'EVENT AND KEY3 = '1') then
				case estado is
					when Fc =>
						--estado <= c1;
					when c1 =>
					when c2 =>
					when Ab =>
						--estado <= c3;

				end case;
			elsif(KEY0'EVENT AND KEY0 = '1') then
				case estado is
					when Fc =>
						if A = '1' then
							estado <= c1;
						end if;
					when c1 =>
						if A = '1' then
							estado <= c2;
						elsif F = '1' then
							estado <= Fc;
						else
							estado <= c1;
						end if;
					when c2 =>
						if A = '1' then
							estado <= Ab;
						elsif F = '1' then
							estado <= c1;
						else
							estado <= c2;
						end if;

					when Ab =>
						if F = '1' then
							estado <= c2;
						end if;
					
				end case;
			end if;	
		end process;
--
--
--
--

		process(estado, KEY3, KEY2) begin
		-- Process Referente à Lógica de Saída do sistema
			if(KEY2 = '1') then
				case estado is
					when Fc =>
					when c1 =>
						A<= not A;
						F<= not F;
					when c2 =>
						A<= not A;
						F<= not F;
					when Ab =>
				end case; 
			elsif(KEY3 = '1') then
				case estado is
					when Fc =>
						A <= '1';
						F <= '0';
					when c1 =>

					when c2 =>

					when Ab =>
						A <= '0';
						F <= '1';
				end case; 
			elsif(KEY0'EVENT and KEY0 = '1') then

				case estado is
					when Fc =>
						if F = '1' then F<= '0'; end if;
						--if(KEY3 = '1') then

						--else
							A<= '0';
							F <= '0';
						--end if;
					when c1 =>

					when c2 =>

					when Ab =>
						if A = '1' then A<= '0'; end if;
						--if(KEY3 = '1') then

						--else
							A<= '0';
							F <= '0';
					--	end if;
					end case;

			end if;
		end process;
			LEDG1<= '1' when estado = Fc else '0';
			LEDG0<= '1' when estado = Ab else '0';
			LEDG7 <= F when estado = c1 or estado = c2 else '0';
--			LEDG7 <= F when estado = c2;--
			LEDG6 <= A when estado = c1 or estado = c2 else '0';
--			LEDG6 <= A when estado = c2;

END ARCHITECTURE;

--PROBLEMAS
----------- 1-> O botão S não desativa após o primeiro clock
----------- 2-> O botão S vai para o SF ou SA quando está no clock 1 ou 3
----------- 3-> Quando acionado o botão S no clock 1, para retornar para o 
----------- SF ou SA, ainda assim leva 3 ticks de clock, quando deveria ser 1
----------- 4-> Ainda é necessário transformar o S em um signal, para armazenar
----------- o sinal do botão físico sem precisar ficar segurando e soltar manualmente
----------- 5-> Botão S quando está em Fc ou Ab
*/
